# Fritzing sketch neo_compass (saved by Fritzing 0.9.2b)
breadboards: 1

parts:
  Part1 = Pro Trinket 5V
  Part2 = Triple Axis Magnetometer - HMC5883 Breakout
  neopixel1 = Neopixel Ring 16

nets:
  GND: Part1.GND, Part2.GND, neopixel1.GND
  VCC: Part1.+5V, Part2.VCC, neopixel1.VCC
  N1: Part1.D6, neopixel1.IN
  N2: Part1.A4, Part2.SDA
  N3: Part1.A5, Part2.SCL

custom parts:
  Pro Trinket 5V: The Pro Trinket 5V is like an Arduino Pro Mini with more pins and USB included. Built with the common core Arduino chip, the ATmega328p, it has 18 GPIO, 2 extra analog inputs, 28K of flash, and 2K of RAM. It has onboard USB bootloading support with Optiboot support, so you can either program your Pro Trinket over USB or with a FTDI cable. The Pro Trinket is programmable using the Arduino IDE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
  Neopixel Ring 16: Neopixel Ring x16
